// Logisim project s-mips.circ as structural Verilog
module S_MIPS_Board (
  input  DESHABILITAR_DISPATCHER,
  output halt
);

  wire button_1_out, CLK, CS, d_ff_1_q, LCLR, LoadRAM, LoadRAMOn, LW, R_R_W, R_W, ram_dispatcher_1_finished,
       RCS, Reset_out, RST, TTY_EN;
  wire [2:0] KDB;
  wire [3:0] LMask, Mask, ram_1_read_time, ram_1_write_time, RMask;
  wire [6:0] KDB_DATA, TTY_DATA;
  wire [15:0] Addr, LAddr, RAddr;
  wire [31:0] I0, I1, I2, I3, LData, ram_1_data_out_0, ram_1_data_out_1, ram_1_data_out_2, ram_1_data_out_3,
       RI0, RI1, RI2, RI3;

  TTY #(.rows(25), .cols(80)) tty_1 (.data(TTY_DATA), .clk(CLK), .we(TTY_EN), .clr(RST));
  not not_1 (LoadRAMOn, ram_dispatcher_1_finished);
  RAM_Dispatcher ram_dispatcher_1 (
    .WriteTime(ram_1_write_time), .Clock(CLK), .Data(LData), .Address(LAddr), .Mask(LMask),
    .Finished(ram_dispatcher_1_finished), .Write(LW), .CLR(LCLR));
  Keyboard #(.buflen(64)) keyboard_1 (.clk(CLK), .re(KDB[0]), .avail(KDB[2]), .data(KDB_DATA));  // open: clr
  RAM_2 ram_1 (
    .Address(RAddr), .Data_Out_0(ram_1_data_out_0), .Data_Out_1(ram_1_data_out_1),
    .Data_Out_2(ram_1_data_out_2), .Data_Out_3(ram_1_data_out_3), .Data_In_0(RI0), .Data_In_1(RI1),
    .Data_In_2(RI2), .Data_In_3(RI3), .Mask(RMask), .nRead_Write(R_R_W), .Chip_Select(RCS),
    .Read_Time(ram_1_read_time), .Reset(button_1_out), .Write_Time(ram_1_write_time));
  Button button_1 (.out(button_1_out));
  D_Flip_Flop d_ff_1 (.clk(CLK), .D(1'b1), .Q(d_ff_1_q), .reset(Reset_out));  // open: Qn, preset, en
  Button Reset (.out(Reset_out));
  S_MIPS s_mips_1 (
    .Kbd_Enable(KDB[0]), .Address(Addr), .Kbd_Clear(KDB[1]), .Kbd_Available(KDB[2]), .RAM_In_0(I0),
    .Kbd_ASCII_Data(KDB_DATA), .RAM_In_1(I1), .TTY_Enable(TTY_EN), .RAM_In_2(I2), .RAM_In_3(I3),
    .TTY_ASCII_Data(TTY_DATA), .Reset(RST), .RAM_Out_0(ram_1_data_out_0), .Clock(CLK),
    .RAM_Out_1(ram_1_data_out_1), .Stop(halt), .RAM_Out_2(ram_1_data_out_2), .RAM_Out_3(ram_1_data_out_3),
    .Mask(Mask), .Read_Time(ram_1_read_time), .Write_Time(ram_1_write_time), .nRead_Write(R_W),
    .Chip_Select(CS));
  D_Flip_Flop d_ff_2 (.clk(CLK), .D(d_ff_1_q), .Qn(LCLR), .reset(Reset_out));  // open: Q, preset, en
  or or_1 (RST, LCLR, LoadRAM);
  Clock clock_1 (.out(CLK));
  Multiplexer #(.width(32), .enable("false")) multiplexer_1 (.in0(I0), .in1(LData), .out(RI0), .sel(LoadRAM));
  Multiplexer #(.width(32), .enable("false")) multiplexer_2 (.in0(I1), .in1(LData), .out(RI1), .sel(LoadRAM));
  Multiplexer #(.width(32), .enable("false")) multiplexer_3 (.in0(I2), .in1(LData), .out(RI2), .sel(LoadRAM));
  Multiplexer #(.width(32), .enable("false")) multiplexer_4 (.in0(I3), .in1(LData), .out(RI3), .sel(LoadRAM));
  and and_1 (LoadRAM, ~DESHABILITAR_DISPATCHER, LoadRAMOn);  // AND_Gate
  Multiplexer #(.width(16), .enable("false")) multiplexer_5 (.in0(Addr), .in1(LAddr), .out(RAddr), .sel(LoadRAM));
  Multiplexer #(.width(4), .enable("false")) multiplexer_6 (.in0(Mask), .in1(LMask), .out(RMask), .sel(LoadRAM));
  Multiplexer #(.enable("false")) multiplexer_7 (.in0(CS), .in1(LW), .out(RCS), .sel(LoadRAM));
  Multiplexer #(.enable("false")) multiplexer_8 (.in0(R_W), .in1(LW), .out(R_R_W), .sel(LoadRAM));

  // Notes on the sheet:
  //   NO MODIFICAR
  //   Keyboard
endmodule

module S_MIPS (
  input  Kbd_Available,
  input  [6:0] Kbd_ASCII_Data,
  input  [31:0] RAM_Out_0,
  input  [31:0] RAM_Out_1,
  input  Reset,
  input  [31:0] RAM_Out_2,
  input  Clock,
  input  [31:0] RAM_Out_3,
  input  [3:0] Read_Time,
  input  [3:0] Write_Time,
  output Kbd_Enable,
  output [15:0] Address,
  output Kbd_Clear,
  output TTY_Enable,
  output [6:0] TTY_ASCII_Data,
  output Stop,
  output [31:0] RAM_In_0,
  output [31:0] RAM_In_1,
  output [31:0] RAM_In_2,
  output [31:0] RAM_In_3,
  output [3:0] Mask,
  output nRead_Write,
  output Chip_Select
);

  wire Exec, halt, is_write, Load_i, mem_needed, pop, PopLoad, push, PushLoad;
  wire [31:0] Data_Read, Instruction, mem_address, mem_write_Data, PC;

  // DATA_PATH data_path_1: pin names not known; wires that end beside it: Load_i, Exec, Instruction, Data_Read, Kbd_ASCII_Data, Kbd_Available, PushLoad, PopLoad, Clock, Reset, Kbd_Enable, pop, push, PC, mem_address, mem_write_Data, halt, mem_needed, is_write, TTY_ASCII_Data, TTY_Enable

  assign Kbd_Clear = Reset;

  // Other names for the same wires on the sheet: CLK = Clock; CS = Chip_Select; KBD_AVAIL = Kbd_Available;
  //   CLR = Reset; KBD_CLR = Reset; KBD_DATA[6:0] = Kbd_ASCII_Data; RAM_A[15:0] = Address;
  //   RAM_INPUT_0[31:0] = RAM_In_0; RAM_INPUT_1[31:0] = RAM_In_1; RAM_INPUT_2[31:0] = RAM_In_2;
  //   RAM_INPUT_3[31:0] = RAM_In_3; RAM_MASK[3:0] = Mask; RAM_OUTPUT_0[31:0] = RAM_Out_0;
  //   RAM_OUTPUT_1[31:0] = RAM_Out_1; RAM_OUTPUT_2[31:0] = RAM_Out_2; RAM_OUTPUT_3[31:0] = RAM_Out_3;
  //   RW = nRead_Write; TTY_DATA[6:0] = TTY_ASCII_Data

  // Notes on the sheet:
  //   RAM ADDRESS
  //   DATA FROM RAM
  //   DATA TO RAM
  //   DATA WRITE MASK
  //   RAM TIMING
  //   RAM CONTROL
  //   KEYBOARD
  //   TTY
  //   SEQUENCING
endmodule

module RAM_2 (
  input  [15:0] Address,
  input  [31:0] Data_In_0,
  input  [31:0] Data_In_1,
  input  [31:0] Data_In_2,
  input  [31:0] Data_In_3,
  input  [3:0] Mask,
  input  nRead_Write,
  input  Chip_Select,
  input  Reset,
  output [31:0] Data_Out_0,
  output [31:0] Data_Out_1,
  output [31:0] Data_Out_2,
  output [31:0] Data_Out_3,
  output [3:0] Read_Time,
  output [3:0] Write_Time
);

  wire and_2_out, and_3_out, and_4_out, and_5_out, and_6_out, and_7_out, and_8_out, and_9_out, Changed, CLK,
       comparator_2_eq, comparator_3_eq, comparator_4_eq, comparator_5_eq, comparator_6_eq, Count,
       demultiplexer_3_out0, Idle, Idle_q, Load, Load0, Load1, nand_1_out, or_1_out, or_2_out, or_3_out,
       or_4_out, or_5_out, or_6_out, or_7_out, or_8_out, or_9_out, or_10_out, Proc_q, Update_Mem, Zero_Time;
  wire [3:0] counter_1_q, multiplexer_1_out, subtractor_1_out;
  wire [31:0] register_1_q, register_2_q, register_3_q, register_4_q, register_5_q;

  // Probe on 4'b0011
  // Probe on 4'b0010
  Multiplexer #(.width(4), .enable("false")) multiplexer_1 (
    .in0(4'b0011), .in1(4'b0010), .out(multiplexer_1_out), .sel(nRead_Write));
  or or_1 (or_1_out, Idle, Update_Mem);
  or or_2 (or_2_out, ~Chip_Select, Reset);  // OR_Gate
  Subtractor #(.width(4)) subtractor_1 (.a(multiplexer_1_out), .b(4'b0010), .out(subtractor_1_out));  // open: bin, bout
  D_Flip_Flop u_Idle (.clk(CLK), .D(or_1_out), .Q(Idle_q), .preset(or_2_out));  // open: Qn, en, reset
  Demultiplexer #(.enable("false")) demultiplexer_1 (.out0(Idle), .out1(Load0), .in(Idle_q), .sel(Changed));
  // Probe on counter_1_q
  Counter #(.width(4), .max('hf)) counter_1 (
    .load(Load), .D(subtractor_1_out), .count(Count), .Q(counter_1_q), .clk(CLK), .clr(or_3_out));  // open: carry
  or or_3 (or_3_out, ~Chip_Select, Reset);  // OR_Gate
  Comparator_part #(.width(4), .mode("unsigned")) comparator_1 (
    .a(4'b0000), .b(counter_1_q), .eq(Zero_Time));  // open: gt, lt
  or or_4 (or_4_out, Count, Load0, Load1);
  Register #(.width(32)) register_1 (.D(Data_In_0), .en(Chip_Select), .Q(register_1_q), .clk(CLK), .clr(or_5_out));
  or or_5 (or_5_out, ~Chip_Select, Reset);  // OR_Gate
  Register #(.width(32)) register_2 (.D(Data_In_1), .en(Chip_Select), .Q(register_2_q), .clk(CLK), .clr(or_6_out));
  or or_6 (or_6_out, ~Chip_Select, Reset);  // OR_Gate
  Register #(.width(32)) register_3 (.D(Data_In_2), .en(Chip_Select), .Q(register_3_q), .clk(CLK), .clr(or_7_out));
  or or_7 (or_7_out, ~Chip_Select, Reset);  // OR_Gate
  Register #(.width(32)) register_4 (.D(Data_In_3), .en(Chip_Select), .Q(register_4_q), .clk(CLK), .clr(or_8_out));
  or or_8 (or_8_out, ~Chip_Select, Reset);  // OR_Gate
  Register #(.width(32)) register_5 (
    .D({{11{1'b1}}, nRead_Write, Mask, Address}), .en(Chip_Select), .Q(register_5_q), .clk(CLK),
    .clr(or_9_out));
  or or_9 (or_9_out, ~Chip_Select, Reset);  // OR_Gate
  D_Flip_Flop Proc (.clk(CLK), .D(or_4_out), .Q(Proc_q), .reset(or_10_out));  // open: Qn, preset, en
  or or_10 (or_10_out, ~Chip_Select, Reset);  // OR_Gate
  Demultiplexer #(.enable("false")) demultiplexer_2 (
    .out0(Count), .out1(Update_Mem), .in(demultiplexer_3_out0), .sel(Zero_Time));
  Demultiplexer #(.enable("false")) demultiplexer_3 (
    .out0(demultiplexer_3_out0), .out1(Load1), .in(Proc_q), .sel(Changed));
  Clock clock_1 (.out(CLK));
  Comparator_part #(.width(32)) comparator_2 (.a(register_1_q), .b(Data_In_0), .eq(comparator_2_eq));  // open: gt, lt
  Comparator_part #(.width(32)) comparator_3 (.a(register_2_q), .b(Data_In_1), .eq(comparator_3_eq));  // open: gt, lt
  Comparator_part #(.width(32)) comparator_4 (.a(register_3_q), .b(Data_In_2), .eq(comparator_4_eq));  // open: gt, lt
  Comparator_part #(.width(32)) comparator_5 (.a(register_4_q), .b(Data_In_3), .eq(comparator_5_eq));  // open: gt, lt
  Comparator_part #(.width(32)) comparator_6 (
    .a(register_5_q), .b({{11{1'b1}}, nRead_Write, Mask, Address}), .eq(comparator_6_eq));  // open: gt, lt
  nand nand_1 (nand_1_out, comparator_6_eq, comparator_2_eq, comparator_3_eq, comparator_4_eq, comparator_5_eq);
  and and_1 (Changed, nand_1_out, Chip_Select);
  or or_11 (Load, Count, Load1, Load0);
  and and_2 (and_2_out, Mask[0], Update_Mem, nRead_Write);
  and and_3 (and_3_out, Mask[1], Update_Mem, nRead_Write);
  and and_4 (and_4_out, Mask[2], Update_Mem, nRead_Write);
  and and_5 (and_5_out, Mask[3], Update_Mem, nRead_Write);
  RAM_part #(.addrWidth(16), .dataWidth(32), .bus("separate")) ram_1 (
    .addr(Address), .din(Data_In_0), .data(Data_Out_0), .str(and_2_out), .sel(Chip_Select), .clk(CLK),
    .ld(and_6_out), .clr(Reset));
  and and_6 (and_6_out, ~nRead_Write, Idle);  // AND_Gate
  RAM_part #(.addrWidth(16), .dataWidth(32), .bus("separate")) ram_2 (
    .addr(Address), .din(Data_In_1), .data(Data_Out_1), .str(and_3_out), .sel(Chip_Select), .clk(CLK),
    .ld(and_7_out), .clr(Reset));
  and and_7 (and_7_out, ~nRead_Write, Idle);  // AND_Gate
  RAM_part #(.addrWidth(16), .dataWidth(32), .bus("separate")) ram_3 (
    .addr(Address), .din(Data_In_2), .data(Data_Out_2), .str(and_4_out), .sel(Chip_Select), .clk(CLK),
    .ld(and_8_out), .clr(Reset));
  and and_8 (and_8_out, ~nRead_Write, Idle);  // AND_Gate
  RAM_part #(.addrWidth(16), .dataWidth(32), .bus("separate")) ram_4 (
    .addr(Address), .din(Data_In_3), .data(Data_Out_3), .str(and_5_out), .sel(Chip_Select), .clk(CLK),
    .ld(and_9_out), .clr(Reset));
  and and_9 (and_9_out, ~nRead_Write, Idle);  // AND_Gate

  assign Read_Time = 4'b0011;
  assign Write_Time = 4'b0010;

  // Other names for the same wires on the sheet: M0 = Mask[0]; M1 = Mask[1]; M2 = Mask[2]; M3 = Mask[3];
  //   RW = nRead_Write; CLR = Reset; CS = Chip_Select; Load2 = Count

  // Notes on the sheet:
  //   NO MODIFICAR
  //   excepto quizás los valores RT y WT
  //   BANK0
  //   BANK1
  //   BANK2
  //   BANK3
endmodule

module RAM_Dispatcher (
  input  [3:0] WriteTime,
  input  Clock,
  input  CLR,
  output [31:0] Data,
  output [15:0] Address,
  output [3:0] Mask,
  output Finished,
  output Write
);

  wire demultiplexer_2_out1, demultiplexer_3_out1, End, IDLE_q, IncAddr, Load, or_1_out, or_2_out, While_q,
       WriteEnd;
  wire [3:0] counter_1_q;
  wire [31:0] CurrentAddress_q;

  Counter #(.width(32), .max('hffffffff)) CurrentAddress (
    .count(IncAddr), .Q({CurrentAddress_q[31:18], Address, CurrentAddress_q[1:0]}), .clk(Clock), .clr(CLR));  // open: load, D, carry
  or or_1 (or_1_out, IncAddr, demultiplexer_3_out1, Finished);
  D_Flip_Flop IDLE (.clk(Clock), .D(or_1_out), .Q(IDLE_q), .preset(CLR));  // open: Qn, en, reset
  Demultiplexer #(.enable("false")) demultiplexer_1 (.out0(Load), .out1(Finished), .in(IDLE_q), .sel(End));
  D_Flip_Flop While (.clk(Clock), .D(or_2_out), .Q(While_q), .reset(CLR));  // open: Qn, preset, en
  or or_2 (or_2_out, Write, Load);
  RAM_part #(.addrWidth(18), .dataWidth(32)) ram_1 (
    .addr({Address, CurrentAddress_q[1:0]}), .data(Data), .clk(Clock));  // open: sel, ld, clr
  Demultiplexer #(.enable("false")) demultiplexer_2 (
    .out0(Write), .out1(demultiplexer_2_out1), .in(While_q), .sel(WriteEnd));
  Decoder #(.select(2)) decoder_1 (
    .out0(Mask[0]), .out1(Mask[1]), .out2(Mask[2]), .out3(Mask[3]), .sel(CurrentAddress_q[1:0]));  // open: en
  Demultiplexer #(.enable("false")) demultiplexer_3 (
    .out0(IncAddr), .out1(demultiplexer_3_out1), .in(demultiplexer_2_out1), .sel(End));
  Counter #(.width(4), .max('hf)) counter_1 (
    .load(Load), .D(WriteTime), .count(Write), .Q(counter_1_q), .clk(Clock));  // open: carry, clr
  Comparator_part #(.width(32)) comparator_1 (.a(Data), .b({32{1'b1}}), .eq(End));  // open: gt, lt
  Comparator_part #(.width(4)) comparator_2 (.a(4'b0000), .b(counter_1_q), .eq(WriteEnd));  // open: gt, lt

  // Other names for the same wires on the sheet: CLK = Clock; Count = Write; WT[3:0] = WriteTime
endmodule

module CONTROL_UNIT (
  input  Start,
  input  Clock,
  input  RST,
  input  [5:0] Op_code,
  input  [5:0] Func_code,
  input  Ready_Inst,
  input  Ready_Data,
  input  Ready_Write,
  output Read_Instruction,
  output Load_Instruction,
  output Read_Data,
  output Write_Data,
  output Register_Enable,
  output Pogram_Counter_Enable,
  output Stack_Pointer_Enable,
  output KBD_Enable,
  output Type_I,
  output MFHI,
  output MFLO,
  output Pop_En,
  output Push_En,
  output Lw_En,
  output Sw_En,
  output KBD,
  output RND,
  output TTY,
  output End
);

  wire ALU, and_1_out, and_2_out, and_3_out, comparator_1_eq, comparator_2_eq, comparator_3_eq,
       comparator_4_eq, comparator_5_eq, comparator_6_eq, comparator_9_eq, comparator_10_eq,
       comparator_11_eq, comparator_12_eq, comparator_13_eq, Cpy, demultiplexer_1_out0, demultiplexer_1_out1,
       demultiplexer_2_out0, demultiplexer_3_out0, demultiplexer_4_out0, Halt, I, IDLE_q, J, Jmp, KBD_t, Lw,
       MFHI_t, MFLO_t, Mry, or_1_out, or_2_out, or_3_out, or_6_out, or_7_out, Pop, Push, R, RND_t, SP1, SP2,
       Spc, Start_Enables, Sw, Tty_t, TtyEn, Wait_3_q, Wait_4_q, Wait_5_q, Wait_8_q, Wait_q;

  and and_1 (and_1_out, Spc, RND_t);
  and and_2 (and_2_out, Spc, KBD_t);
  and and_3 (and_3_out, Spc, Halt);
  Demultiplexer #(.enable("false")) demultiplexer_1 (
    .out0(demultiplexer_1_out0), .out1(demultiplexer_1_out1), .in(IDLE_q), .sel(Start));
  D_Flip_Flop #(.trigger("falling")) IDLE (
    .clk(Clock), .D(demultiplexer_1_out0), .Q(IDLE_q), .preset(RST));  // open: Qn, en, reset
  or or_1 (or_1_out, ALU, Cpy, Ready_Data, and_1_out, and_2_out);
  D_Flip_Flop #(.trigger("falling")) Wait (.clk(Clock), .D(Mry), .Q(Wait_q), .reset(RST));  // open: Qn, preset, en
  Demultiplexer #(.enable("false")) demultiplexer_2 (
    .out0(demultiplexer_2_out0), .out1(Read_Data), .in(Wait_q), .sel(or_3_out));
  or or_2 (or_2_out, End, and_3_out);
  D_Flip_Flop #(.trigger("falling")) Wait_2 (
    .clk(Clock), .D(or_1_out), .Q(Register_Enable), .reset(RST));  // open: Qn, preset, en
  or or_3 (or_3_out, Lw, Pop);
  D_Flip_Flop #(.trigger("falling")) u_End (.clk(Clock), .D(or_2_out), .Q(End), .reset(RST));  // open: Qn, preset, en
  or or_4 (Read_Instruction, demultiplexer_1_out1, Pogram_Counter_Enable);
  Demultiplexer #(.enable("false")) demultiplexer_3 (
    .out0(demultiplexer_3_out0), .out1(SP2), .in(demultiplexer_2_out0), .sel(Push));
  D_Flip_Flop #(.trigger("falling")) Wait_3 (
    .clk(Clock), .D(Register_Enable), .Q(Wait_3_q), .reset(RST));  // open: Qn, preset, en
  Demultiplexer #(.enable("false")) demultiplexer_4 (.out0(demultiplexer_4_out0), .out1(SP1), .in(Wait_3_q), .sel(Pop));
  and and_4 (TtyEn, Spc, Tty_t);
  and and_5 (KBD_Enable, KBD_t, demultiplexer_4_out0);
  or or_5 (Write_Data, demultiplexer_3_out0, Wait_4_q);
  D_Flip_Flop #(.trigger("falling")) Wait_4 (.clk(Clock), .D(SP2), .Q(Wait_4_q), .reset(RST));  // open: Qn, preset, en
  or or_6 (or_6_out, demultiplexer_4_out0, Wait_5_q);
  D_Flip_Flop #(.trigger("falling")) Wait_5 (.clk(Clock), .D(SP1), .Q(Wait_5_q), .reset(RST));  // open: Qn, preset, en
  D_Flip_Flop #(.trigger("falling")) Wait_6 (
    .clk(Clock), .D(Ready_Inst), .Q(Start_Enables), .reset(RST));  // open: Qn, preset, en
  D_Flip_Flop #(.trigger("falling")) Wait_7 (
    .clk(Clock), .D(or_7_out), .Q(Pogram_Counter_Enable), .reset(RST));  // open: Qn, preset, en
  or or_7 (or_7_out, or_6_out, Jmp, Ready_Write, TtyEn);
  Operation_Decoder operation_decoder_1 (
    .Op_code(Op_code), .Func_code(Func_code), .Type_R(R), .Type_I(I), .Type_J(J), .Copy_Inst(Cpy),
    .Jump_Inst(Jmp), .Memory_Inst(Mry), .Special_Inst(Spc), .ALU_Inst(ALU), .Enable(Start_Enables));
  Comparator_part #(.width(6)) comparator_1 (.a(Op_code), .b({6{1'b0}}), .eq(comparator_1_eq));  // open: gt, lt
  Comparator_part #(.width(6)) comparator_2 (.a(Func_code), .b(6'b010010), .eq(comparator_2_eq));  // open: gt, lt
  and and_6 (MFLO_t, comparator_2_eq, comparator_1_eq);
  and and_7 (MFHI_t, comparator_1_eq, comparator_3_eq);
  Comparator_part #(.width(6)) comparator_3 (.a(Func_code), .b(6'b010000), .eq(comparator_3_eq));  // open: gt, lt
  Comparator_part #(.width(6)) comparator_4 (.a(Op_code), .b(6'b111000), .eq(comparator_4_eq));  // open: gt, lt
  and and_8 (Pop, comparator_4_eq, comparator_5_eq);
  Comparator_part #(.width(6)) comparator_5 (.a(Func_code), .b({6{1'b0}}), .eq(comparator_5_eq));  // open: gt, lt
  and and_9 (Push, comparator_4_eq, comparator_6_eq);
  Comparator_part #(.width(6)) comparator_6 (.a(Func_code), .b(6'b000001), .eq(comparator_6_eq));  // open: gt, lt
  Comparator_part #(.width(6)) comparator_7 (.a(Op_code), .b(6'b100011), .eq(Lw));  // open: gt, lt
  Comparator_part #(.width(6)) comparator_8 (.a(Op_code), .b(6'b101011), .eq(Sw));  // open: gt, lt
  Comparator_part #(.width(6)) comparator_9 (.a(Op_code), .b({6{1'b1}}), .eq(comparator_9_eq));  // open: gt, lt
  and and_10 (RND_t, comparator_9_eq, comparator_10_eq);
  Comparator_part #(.width(6)) comparator_10 (.a(Func_code), .b(6'b000010), .eq(comparator_10_eq));  // open: gt, lt
  and and_11 (KBD_t, comparator_9_eq, comparator_11_eq);
  Comparator_part #(.width(6)) comparator_11 (.a(Func_code), .b(6'b000100), .eq(comparator_11_eq));  // open: gt, lt
  and and_12 (Tty_t, comparator_9_eq, comparator_12_eq);
  Comparator_part #(.width(6)) comparator_12 (.a(Func_code), .b(6'b000001), .eq(comparator_12_eq));  // open: gt, lt
  and and_13 (Halt, comparator_9_eq, comparator_13_eq);
  Comparator_part #(.width(6)) comparator_13 (.a(Func_code), .b({6{1'b1}}), .eq(comparator_13_eq));  // open: gt, lt
  or or_8 (Stack_Pointer_Enable, SP2, SP1);
  and and_14 (Type_I, I, Wait_8_q);
  and and_15 (MFHI, MFHI_t, Wait_8_q);
  and and_16 (MFLO, MFLO_t, Wait_8_q);
  and and_17 (Pop_En, Pop, Wait_8_q);
  and and_18 (Push_En, Push, Wait_8_q);
  and and_19 (Lw_En, Lw, Wait_8_q);
  and and_20 (Sw_En, Sw, Wait_8_q);
  and and_21 (KBD, KBD_t, Wait_8_q);
  and and_22 (RND, RND_t, Wait_8_q);
  and and_23 (TTY, TtyEn, Wait_8_q);
  D_Flip_Flop #(.trigger("falling")) Wait_8 (
    .clk(Clock), .Q(Wait_8_q), .preset(Start_Enables), .reset(Pogram_Counter_Enable));  // open: D, Qn, en

  assign Load_Instruction = Ready_Inst;

  // Other names for the same wires on the sheet: CLK = Clock; CLR = RST; Load_Inst = Ready_Inst;
  //   Read_Inst = Read_Instruction; RegEN = Register_Enable; SPEN = Stack_Pointer_Enable;
  //   PCEN = Pogram_Counter_Enable; Stop_Enables = Pogram_Counter_Enable

  // Notes on the sheet:
  //   Flags
endmodule

module Operation_Decoder (
  input  [5:0] Op_code,
  input  [5:0] Func_code,
  input  Enable,
  output Type_R,
  output Type_I,
  output Type_J,
  output Copy_Inst,
  output Jump_Inst,
  output Memory_Inst,
  output Special_Inst,
  output ALU_Inst
);

  wire _000000, _111000, _111111, and_3_out, and_4_out, and_5_out, and_6_out, and_7_out, comparator_1_eq,
       comparator_5_eq, comparator_6_eq, comparator_7_eq, comparator_8_eq, comparator_9_lt, comparator_10_eq,
       comparator_11_eq, nor_1_out, not_1_out, not_2_out, or_2_out, or_3_out, or_4_out;

  not not_1 (not_1_out, Type_R);
  not not_2 (not_2_out, comparator_1_eq);
  Comparator_part #(.width(6)) comparator_1 (.a(Op_code), .b(6'b000010), .eq(comparator_1_eq));  // open: gt, lt
  or or_1 (Type_R, _000000, _111000, _111111);
  and and_1 (Type_I, not_2_out, not_1_out);
  and and_2 (Type_J, comparator_1_eq, not_1_out);
  Comparator_part #(.width(6)) comparator_2 (.a(Op_code), .b({6{1'b0}}), .eq(_000000));  // open: gt, lt
  Comparator_part #(.width(6)) comparator_3 (.a(Op_code), .b(6'b111000), .eq(_111000));  // open: gt, lt
  Comparator_part #(.width(6)) comparator_4 (.a(Op_code), .b({6{1'b1}}), .eq(_111111));  // open: gt, lt
  Comparator_part #(.width(6)) comparator_5 (.a(Func_code), .b(6'b010010), .eq(comparator_5_eq));  // open: gt, lt
  and and_3 (and_3_out, comparator_5_eq, _000000);
  and and_4 (and_4_out, _000000, comparator_6_eq);
  Comparator_part #(.width(6)) comparator_6 (.a(Func_code), .b(6'b010000), .eq(comparator_6_eq));  // open: gt, lt
  Comparator_part #(.width(6)) comparator_7 (.a(Func_code), .b({6{1'b0}}), .eq(comparator_7_eq));  // open: gt, lt
  and and_5 (and_5_out, comparator_7_eq, _000000);
  and and_6 (and_6_out, _000000, comparator_8_eq);
  Comparator_part #(.width(6)) comparator_8 (.a(Func_code), .b(6'b001000), .eq(comparator_8_eq));  // open: gt, lt
  and and_7 (and_7_out, comparator_9_lt, Type_I);
  Comparator_part #(.width(6), .mode("unsigned")) comparator_9 (
    .a(Op_code), .b(6'b001000), .lt(comparator_9_lt));  // open: gt, eq
  Comparator_part #(.width(6)) comparator_10 (.a(Op_code), .b(6'b100011), .eq(comparator_10_eq));  // open: gt, lt
  Comparator_part #(.width(6)) comparator_11 (.a(Op_code), .b(6'b101011), .eq(comparator_11_eq));  // open: gt, lt
  or or_2 (or_2_out, and_3_out, and_4_out);
  or or_3 (or_3_out, and_5_out, and_6_out, and_7_out);
  or or_4 (or_4_out, _111000, comparator_10_eq, comparator_11_eq);
  nor nor_1 (nor_1_out, Copy_Inst, Jump_Inst, Memory_Inst, Special_Inst);
  and and_8 (Copy_Inst, Enable, or_2_out);
  and and_9 (Jump_Inst, Enable, or_3_out);
  and and_10 (Memory_Inst, Enable, or_4_out);
  and and_11 (Special_Inst, Enable, _111111);
  and and_12 (ALU_Inst, Enable, nor_1_out);

  // Other names for the same wires on the sheet: EN = Enable
endmodule

module DATA_PATH (
  input  Clock,
  input  [31:0] KBD_Input,
  input  Reset,
  input  [31:0] Instruction,
  input  Instruction_Enable,
  input  Type_I,
  input  Register_Enable,
  input  Program_Counter_Enable,
  input  Save_Word_Enable,
  input  Load_Word_Enable,
  input  MFHI,
  input  MFLO,
  input  Push,
  input  Pop,
  input  SP_Write,
  input  RND,
  input  KBD,
  output [5:0] Op_code,
  output [5:0] Func_code,
  output [31:0] RS___RT,
  output [31:0] Memory_Address,
  output [6:0] TtyOutput
);

  wire instruction_1_p6, Sign;
  wire [3:0] alu_control_1_selector;
  wire [4:0] multiplexer_2_out, RD, RT;
  wire [15:0] Const;
  wire [25:0] Destine;
  wire [31:0] ALUOut, Const_star, Hi, Lo, multiplexer_1_out, PC, PC_star, random_1_out, RT_t, SP;
  wire [31:7] RS_t;

  // Instruction instruction_1: pin names not known; wires that end beside it: Instruction, PC, Clock, Reset, Instruction_Enable, instruction_1_p6, instruction_1_p6
  // Program_Counter program_counter_1: pin names not known; wires that end beside it: PC_star, Program_Counter_Enable, Clock, Reset, PC
  Branch_Control branch_control_1 (.Next_PC(PC_star));  // open: PC, offset, Address, Register_Value, Zero, Sng, BLEZ, BGTZ, BLTZ, BEQ, BNE, J, Jr
  // Instruction_Decoder instruction_decoder_1: pin names not known; wires that end beside it: RD, Destine, Const, Op_code, Func_code
  Multiplexer #(.width(32), .enable("false")) multiplexer_1 (
    .in0(RT_t), .in1(Const_star), .out(multiplexer_1_out), .sel(Type_I));
  Random #(.width(32)) random_1 (.clk(Clock), .out(random_1_out));  // open: next, clr
  ALU alu_1 (
    .in_4(Sign), .Input({RS_t, TtyOutput}), .Input_2(multiplexer_1_out), .in_3(alu_control_1_selector),
    .Output(ALUOut), .LO(Lo), .HI(Hi), .in_5(Clock));
  ALU_Control alu_control_1 (
    .Op_code(Op_code), .Func_code(Func_code), .Sign(Sign), .Selector(alu_control_1_selector), .Const(Const),
    .Const_Extended(Const_star));
  Multiplexer #(.width(5), .enable("false")) multiplexer_2 (.in0(RD), .in1(RT), .out(multiplexer_2_out), .sel(Type_I));
  Register_File register_file_1 (
    .OutA({RS_t, TtyOutput}), .Lo_out(RT_t));  // open: DataIncome, DataAddress, Selector_A, Selector_B, Hi_in, Lo_in, Reset, Clock, in_9, WriteEnable, OutB, Hi_out, SP
  Multiplexer #(.width(32), .enable("false")) multiplexer_3 (
    .in0({RS_t, TtyOutput}), .in1(RT_t), .out(RS___RT), .sel(Save_Word_Enable));
  // Memory_Address memory_address_1: pin names not known; wires that end beside it: Register_Enable, Push, Pop, SP, PC, SP, ALUOut, Load_Word_Enable, Push, Save_Word_Enable, Pop, Memory_Address

  // Other names for the same wires on the sheet: CLK = Clock; CLR = Reset; I = Type_I; InstEN = Instruction_Enable;
  //   LwEN = Load_Word_Enable; PCEN = Program_Counter_Enable; RegEN = Register_Enable; RS_t[6:0] = TtyOutput;
  //   SwEN = Save_Word_Enable

  // Notes on the sheet:
  //   Flags
endmodule

module Branch_Control (
  input  [31:0] PC,
  input  [15:0] offset,
  input  [25:0] Address,
  input  [31:0] Register_Value,
  input  Zero,
  input  Sng,
  input  BLEZ,
  input  BGTZ,
  input  BLTZ,
  input  BEQ,
  input  BNE,
  input  J,
  input  Jr,
  output [31:0] Next_PC
);

  wire and_1_out, and_2_out, and_3_out, and_4_out, and_5_out, and_6_out, or_1_out, sel;
  wire [31:0] multiplexer_1_out, multiplexer_2_out, PC_4, PC_4_4_offset;
  wire [31:18] sng_extend_offset_____2;

  or or_1 (or_1_out, Sng, Zero);
  and and_1 (and_1_out, BEQ, Zero);
  and and_2 (and_2_out, BLEZ, or_1_out);
  Multiplexer #(.width(32), .enable("false")) multiplexer_1 (
    .in0(PC_4), .in1(PC_4_4_offset), .out(multiplexer_1_out), .sel(sel));
  and and_3 (and_3_out, BNE, ~Zero);  // AND_Gate
  and and_4 (and_4_out, BGTZ, and_5_out);
  and and_5 (and_5_out, ~Sng, ~Zero);  // AND_Gate
  Multiplexer #(.width(32), .enable("false")) multiplexer_2 (
    .in0(multiplexer_1_out), .in1(Register_Value), .out(multiplexer_2_out), .sel(Jr));
  and and_6 (and_6_out, BLTZ, Sng);
  Multiplexer #(.width(32), .enable("false")) multiplexer_3 (
    .in0(multiplexer_2_out), .in1({PC[31:28], Address, 2'b00}), .out(Next_PC), .sel(J));
  or or_2 (sel, and_1_out, and_3_out, and_2_out, and_4_out, and_6_out);
  Adder #(.width(32)) adder_1 (.a(PC), .b(32'h4), .out(PC_4));  // open: cin, cout
  assign sng_extend_offset_____2 = {{13{offset[15]}}, offset[15]};  // Bit_Extender bit_extender_1
  Adder #(.width(32)) adder_2 (
    .a(PC_4), .b({sng_extend_offset_____2, offset, 2'b00}), .out(PC_4_4_offset));  // open: cin, cout

  // Other names for the same wires on the sheet: Destine[31:2] = {PC[31:28], Address}; Next[31:0] = Next_PC;
  //   RV[31:0] = Register_Value; sng_extend_offset_____2[17:2] = offset; Z = Zero

  // Notes on the sheet:
  //   Input
  //   Sub Case Selection 
  //   Output
  //   Calculate operation
endmodule

module Program_Counter (
  input  [31:0] PC_New,
  input  Enable,
  input  Clk,
  input  RST,
  output [31:0] PC_Actual
);

  Register #(.width(32)) register_1 (.D(PC_New), .en(Enable), .Q(PC_Actual), .clk(Clk), .clr(RST));
endmodule

module ALU (
  input  [31:0] Input,
  input  [31:0] Input_2,
  input  [3:0] in_3,
  input  in_4,
  input  in_5,
  output [31:0] Output,
  output [31:0] LO,
  output [31:0] HI
);

  wire div, enable, mul;
  wire [31:0] add, \and , div_rem, div_res, mul_HI, mul_LO, multiplexer_2_out, multiplexer_3_out, \nand ,
       \nor , \or , slt, sub, \xor ;

  assign \and  = Input & Input_2;  // AND_Gate and_1, 32 bits wide
  assign \or  = Input | Input_2;  // OR_Gate or_1, 32 bits wide
  assign \nand  = ~(Input & Input_2);  // NAND_Gate nand_1, 32 bits wide
  assign \nor  = ~(Input | Input_2);  // NOR_Gate nor_1, 32 bits wide
  assign \xor  = Input ^ Input_2;  // XOR_Gate xor_1, 32 bits wide
  Adder #(.width(32)) adder_1 (.a(Input), .b(Input_2), .out(add));  // open: cin, cout
  Subtractor #(.width(32)) subtractor_1 (.a(Input), .b(Input_2), .out(sub));  // open: bin, bout
  Divider divider_1 (.in_1(Input), .in_3(in_4), .in_2(Input_2), .Result(div_res), .Remainder(div_rem));
  Multiplier multiplier_1 (.in_1(Input), .in_3(in_4), .in_2(Input_2), .Output(mul_HI), .Output_2(mul_LO));
  Comparator comparator_1 (.in_1(Input), .in_3(in_4), .in_2(Input_2), .Output(slt));
  Multiplexer #(.select(4), .width(32), .enable("false")) multiplexer_1 (
    .in0(add), .in1(sub), .in4(slt), .in5(\and ), .in6(\or ), .in7(\nor ), .in8(\xor ), .out(Output),
    .sel(in_3));  // open: in2, in3, in9, in10, in11, in12, in13, in14, in15
  and and_2 (mul, ~in_3[0], in_3[1], ~in_3[2], ~in_3[3]);  // AND_Gate
  and and_3 (div, in_3[0], in_3[1], ~in_3[2], ~in_3[3]);  // AND_Gate
  or or_2 (enable, mul, div);
  Multiplexer #(.width(32), .enable("false")) multiplexer_2 (
    .in0(mul_LO), .in1(div_res), .out(multiplexer_2_out), .sel(div));
  Multiplexer #(.width(32), .enable("false")) multiplexer_3 (
    .in0(mul_HI), .in1(div_rem), .out(multiplexer_3_out), .sel(div));
  Register #(.width(32)) register_1 (.D(multiplexer_2_out), .en(enable), .Q(LO), .clk(in_5));  // open: clr
  Register #(.width(32)) register_2 (.D(multiplexer_3_out), .en(enable), .Q(HI), .clk(in_5));  // open: clr

  // Other names for the same wires on the sheet: a[31:0] = Input; b[31:0] = Input_2; clock = in_5; _0 = in_3[0];
  //   selector[3:0] = in_3; _1 = in_3[1]; _2 = in_3[2]; _3 = in_3[3]; sign = in_4
endmodule

module ALU_Control (
  input  [15:0] Const,
  input  [5:0] Op_code,
  input  [5:0] Func_code,
  output Sign,
  output [3:0] Selector,
  output [31:0] Const_Extended
);

  wire Add, AddI, And, AndI, comparator_1_eq, comparator_2_eq, comparator_3_eq, comparator_4_eq,
       comparator_5_eq, comparator_6_eq, comparator_7_eq, comparator_8_eq, comparator_9_eq, comparator_10_eq,
       comparator_11_eq, comparator_12_eq, comparator_13_eq, Div, DivU, Lw, Mult, MultU, Nor, Or, or_1_out,
       OrI, Slt, SltU, StlI, StlIU, Sub, Sw, Xor, XorI;

  Comparator_part #(.width(6)) comparator_1 (.a(Op_code), .b({6{1'b0}}), .eq(comparator_1_eq));  // open: gt, lt
  Comparator_part #(.width(6)) comparator_2 (.a(Func_code), .b(6'b100000), .eq(comparator_2_eq));  // open: gt, lt
  Comparator_part #(.width(6)) comparator_3 (.a(Func_code), .b(6'b100010), .eq(comparator_3_eq));  // open: gt, lt
  Comparator_part #(.width(6)) comparator_4 (.a(Func_code), .b(6'b011000), .eq(comparator_4_eq));  // open: gt, lt
  Comparator_part #(.width(6)) comparator_5 (.a(Func_code), .b(6'b011001), .eq(comparator_5_eq));  // open: gt, lt
  Comparator_part #(.width(6)) comparator_6 (.a(Func_code), .b(6'b011010), .eq(comparator_6_eq));  // open: gt, lt
  Comparator_part #(.width(6)) comparator_7 (.a(Func_code), .b(6'b011011), .eq(comparator_7_eq));  // open: gt, lt
  Comparator_part #(.width(6)) comparator_8 (.a(Func_code), .b(6'b100100), .eq(comparator_8_eq));  // open: gt, lt
  Comparator_part #(.width(6)) comparator_9 (.a(Func_code), .b(6'b100101), .eq(comparator_9_eq));  // open: gt, lt
  Comparator_part #(.width(6)) comparator_10 (.a(Func_code), .b(6'b100111), .eq(comparator_10_eq));  // open: gt, lt
  Comparator_part #(.width(6)) comparator_11 (.a(Func_code), .b(6'b101000), .eq(comparator_11_eq));  // open: gt, lt
  Comparator_part #(.width(6)) comparator_12 (.a(Func_code), .b(6'b101010), .eq(comparator_12_eq));  // open: gt, lt
  Comparator_part #(.width(6)) comparator_13 (.a(Func_code), .b(6'b101011), .eq(comparator_13_eq));  // open: gt, lt
  and and_1 (Add, comparator_1_eq, comparator_2_eq);
  and and_2 (Sub, comparator_1_eq, comparator_3_eq);
  and and_3 (Mult, comparator_1_eq, comparator_4_eq);
  and and_4 (MultU, comparator_1_eq, comparator_5_eq);
  and and_5 (Div, comparator_1_eq, comparator_6_eq);
  and and_6 (DivU, comparator_1_eq, comparator_7_eq);
  and and_7 (And, comparator_1_eq, comparator_8_eq);
  and and_8 (Or, comparator_1_eq, comparator_9_eq);
  and and_9 (Nor, comparator_1_eq, comparator_10_eq);
  and and_10 (Xor, comparator_1_eq, comparator_11_eq);
  and and_11 (Slt, comparator_1_eq, comparator_12_eq);
  and and_12 (SltU, comparator_1_eq, comparator_13_eq);
  Comparator_part #(.width(6)) comparator_14 (.a(Op_code), .b(6'b001000), .eq(AddI));  // open: gt, lt
  Comparator_part #(.width(6)) comparator_15 (.a(Op_code), .b(6'b001100), .eq(AndI));  // open: gt, lt
  Comparator_part #(.width(6)) comparator_16 (.a(Op_code), .b(6'b001101), .eq(OrI));  // open: gt, lt
  Comparator_part #(.width(6)) comparator_17 (.a(Op_code), .b(6'b001110), .eq(XorI));  // open: gt, lt
  Comparator_part #(.width(6)) comparator_18 (.a(Op_code), .b(6'b001010), .eq(StlI));  // open: gt, lt
  Comparator_part #(.width(6)) comparator_19 (.a(Op_code), .b(6'b001011), .eq(StlIU));  // open: gt, lt
  Comparator_part #(.width(6)) comparator_20 (.a(Op_code), .b(6'b100011), .eq(Lw));  // open: gt, lt
  Comparator_part #(.width(6)) comparator_21 (.a(Op_code), .b(6'b101011), .eq(Sw));  // open: gt, lt
  or or_1 (or_1_out, Lw, AddI, Sw);
  and and_13 (Const_Extended[31], Const[15], ~AndI, ~OrI, ~XorI);  // AND_Gate
  ALU_Encoder alu_encoder_1 (
    .in_1(Add), .in_2(Sub), .in_3(Mult), .in_4(MultU), .in_5(Div), .in_6(DivU), .in_7(Slt), .in_8(SltU),
    .in_9(And), .in_10(Or), .in_11(Nor), .in_12(Xor), .in_13(or_1_out), .in_14(StlI), .in_15(StlIU),
    .in_16(AndI), .in_17(OrI), .in_18(XorI), .sign(Sign), .selector(Selector));  // open: I

  assign Const_Extended[30:0] = {{15{Const_Extended[31]}}, Const};
endmodule

module ALU_Encoder (
  input  in_1,
  input  in_2,
  input  in_3,
  input  in_4,
  input  in_5,
  input  in_6,
  input  in_7,
  input  in_8,
  input  in_9,
  input  in_10,
  input  in_11,
  input  in_12,
  input  in_13,
  input  in_14,
  input  in_15,
  input  in_16,
  input  in_17,
  input  in_18,
  output sign,
  output I,
  output [3:0] selector
);

  wire AND, DIV, MUL, OR, SLT, SLTI;

  or or_1 (MUL, in_3, in_4);
  or or_2 (DIV, in_5, in_6);
  or or_3 (SLT, in_7, in_8);
  or or_4 (SLTI, in_14, in_15);
  or or_5 (AND, in_9, in_16);
  or or_6 (OR, in_10, in_17);
  or or_7 (selector[3], in_12, in_18);
  or or_8 (selector[0], in_2, DIV, AND, in_11);
  or or_9 (selector[1], MUL, DIV, OR, in_11);
  or or_10 (selector[2], SLT, SLTI, OR, AND, in_11);
  or or_11 (sign, in_3, in_5, in_7, in_14);
  or or_12 (I, in_13, SLTI, in_16, in_17, in_18);

  // Other names for the same wires on the sheet: add = in_1; addi = in_13; and_t = in_9; andi = in_16; div_t = in_5;
  //   divu = in_6; mul_t = in_3; mulu = in_4; nor = in_11; or_t = in_10; ori = in_17; _0 = selector[0];
  //   _1 = selector[1]; _2 = selector[2]; _3 = selector[3]; XOR = selector[3]; slt_t = in_7; slti_t = in_14;
  //   sltiu = in_15; sltu = in_8; sub = in_2; xor_t = in_12; xori = in_18
endmodule

module Comparator (
  input  [31:0] in_1,
  input  [31:0] in_2,
  input  in_3,
  output [31:0] Output
);

  wire multiplexer_1_out, slt, sltu;

  Comparator_part #(.width(32)) comparator_1 (.a(in_1), .b(in_2), .lt(slt));  // open: gt, eq
  Comparator_part #(.width(32), .mode("unsigned")) comparator_2 (.a(in_1), .b(in_2), .lt(sltu));  // open: gt, eq
  Multiplexer #(.enable("false")) multiplexer_1 (.in0(sltu), .in1(slt), .out(multiplexer_1_out), .sel(in_3));
  assign Output = {{31{1'b0}}, multiplexer_1_out};  // Bit_Extender bit_extender_1

  // Other names for the same wires on the sheet: a[31:0] = in_1; b[31:0] = in_2; sign = in_3
endmodule

module Divider (
  input  [31:0] in_1,
  input  [31:0] in_2,
  input  in_3,
  output [31:0] Result,
  output [31:0] Remainder
);

  wire negative_a, negative_b, negative_result;
  wire [31:0] abs_a, abs_b, abs_result, adder_1_out, divider_1_out, multiplexer_1_out, negator_1_out,
       negator_2_out, negator_3_out, negator_4_out, rem, subtractor_1_out;

  Divider_part #(.width(32)) divider_1 (.a(abs_a), .b(abs_b), .out(divider_1_out), .rem(rem));  // open: upper
  xor xor_1 (negative_result, negative_a, negative_b);
  and and_1 (negative_a, in_1[31], in_3);
  and and_2 (negative_b, in_3, in_2[31]);
  Adder #(.width(32)) adder_1 (.a(divider_1_out), .b(32'h1), .out(adder_1_out));  // open: cin, cout
  Multiplexer #(.width(32), .enable("false")) multiplexer_1 (
    .in0(divider_1_out), .in1(adder_1_out), .out(multiplexer_1_out), .sel(negative_a));
  Negator #(.width(32)) negator_1 (.in(in_1), .out(negator_1_out));
  Negator #(.width(32)) negator_2 (.in(in_2), .out(negator_2_out));
  Multiplexer #(.width(32), .enable("false")) multiplexer_2 (
    .in0(multiplexer_1_out), .in1(negator_3_out), .out(Result), .sel(negative_result));
  Negator #(.width(32)) negator_3 (.in(multiplexer_1_out), .out(negator_3_out));
  Negator #(.width(32)) negator_4 (.in(abs_result), .out(negator_4_out));
  Multiplexer #(.width(32), .enable("false")) multiplexer_3 (
    .in0(in_1), .in1(negator_1_out), .out(abs_a), .sel(negative_a));
  Multiplexer #(.width(32), .enable("false")) multiplexer_4 (
    .in0(in_2), .in1(negator_2_out), .out(abs_b), .sel(negative_b));
  Multiplexer #(.width(32), .enable("false")) multiplexer_5 (
    .in0(abs_result), .in1(negator_4_out), .out(Result), .sel(negative_result));
  Subtractor #(.width(32)) subtractor_1 (.a(abs_b), .b(rem), .out(subtractor_1_out));  // open: bin, bout
  Multiplexer #(.width(32), .enable("false")) multiplexer_6 (
    .in0(rem), .in1(subtractor_1_out), .out(Remainder), .sel(negative_a));

  // Other names for the same wires on the sheet: a[31:0] = in_1; b[31:0] = in_2; sign = in_3
endmodule

module Multiplier (
  input  [31:0] in_1,
  input  [31:0] in_2,
  input  in_3,
  output [31:0] Output,
  output [31:0] Output_2
);

  wire adder_1_cout, adder_3_cout, adder_5_cout, and_2_out, c1, c2, ca, cb;
  wire [31:0] a_2, a_cb, adder_1_out, adder_2_out, adder_3_out, adder_4_out, and_1_out, and_3_out, b_2, b_ca,
       bit_extender_1_out, bit_extender_2_out, c_ab, HI, HIU, LO, LOU, multiplier_1_cout, multiplier_1_out,
       shift_left_3_out_3, shift_left_4_out_3, shift_left_5_out_3, shift_left_out_3;

  Shift_Right shift_right_1 (.in_1(in_1), .out_4(a_2), .Output(ca), .in_2(1'b0));
  assign and_1_out = a_2 & bit_extender_1_out;  // AND_Gate and_1, 32 bits wide
  assign bit_extender_1_out = {{31{cb}}, cb};  // Bit_Extender bit_extender_1
  Multiplier_part #(.width(32)) multiplier_1 (
    .a(a_2), .b(b_2), .out(multiplier_1_out), .cout(multiplier_1_cout));  // open: cin
  Shift_Left shift_left (.in_2(multiplier_1_out), .out_3(shift_left_out_3), .Output(c1), .in_1(1'b0));
  Shift_Right shift_right_2 (.in_1(in_2), .out_4(b_2), .Output(cb), .in_2(1'b0));
  Shift_Left shift_left_2 (.in_2(and_1_out), .out_3(a_cb), .in_1(1'b0));  // open: Output
  Shift_Left shift_left_3 (.in_2(shift_left_out_3), .out_3(shift_left_3_out_3), .Output(c2), .in_1(1'b0));
  Shift_Left shift_left_4 (.in_2(multiplier_1_cout), .out_3(shift_left_4_out_3), .in_1(c1));  // open: Output
  Shift_Left shift_left_5 (.in_2(shift_left_4_out_3), .out_3(shift_left_5_out_3), .in_1(c2));  // open: Output
  and and_2 (and_2_out, ca, cb);
  assign bit_extender_2_out = {{31{ca}}, ca};  // Bit_Extender bit_extender_2
  Adder #(.width(32)) adder_1 (.a(shift_left_3_out_3), .b(a_cb), .out(adder_1_out), .cout(adder_1_cout));  // open: cin
  Adder #(.width(32)) adder_2 (
    .a(shift_left_5_out_3), .b({32{1'b0}}), .out(adder_2_out), .cin(adder_1_cout));  // open: cout
  assign c_ab = {{31{1'b0}}, and_2_out};  // Bit_Extender bit_extender_3
  assign and_3_out = b_2 & bit_extender_2_out;  // AND_Gate and_3, 32 bits wide
  Adder #(.width(32)) adder_3 (.a(adder_1_out), .b(b_ca), .out(adder_3_out), .cout(adder_3_cout));  // open: cin
  Adder #(.width(32)) adder_4 (.a(adder_2_out), .b({32{1'b0}}), .out(adder_4_out), .cin(adder_3_cout));  // open: cout
  Shift_Left shift_left_6 (.in_2(and_3_out), .out_3(b_ca), .in_1(1'b0));  // open: Output
  Adder #(.width(32)) adder_5 (.a(adder_3_out), .b(c_ab), .out(LOU), .cout(adder_5_cout));  // open: cin
  Adder #(.width(32)) adder_6 (.a(adder_4_out), .b({32{1'b0}}), .out(HIU), .cin(adder_5_cout));  // open: cout
  Multiplexer #(.width(32), .enable("false")) multiplexer_1 (.in0(HIU), .in1(HI), .out(Output), .sel(in_3));
  Multiplexer #(.width(32), .enable("false")) multiplexer_2 (.in0(LOU), .in1(LO), .out(Output_2), .sel(in_3));
  Multiplier_part #(.width(32)) multiplier_2 (.a(in_1), .b(in_2), .out(LO), .cout(HI));  // open: cin

  // Other names for the same wires on the sheet: a[31:0] = in_1; b[31:0] = in_2; sign = in_3
endmodule

module Shift_Right (
  input  [31:0] in_1,
  input  in_2,
  output Output,
  output [31:0] out_4
);


  assign out_4 = {in_2, in_1[31:1]};
  assign Output = in_1[0];

  // Other names for the same wires on the sheet: a[31:0] = in_1; a____1[31:0] = {in_2, in_1[31:1]}
endmodule

module Shift_Left (
  input  in_1,
  input  [31:0] in_2,
  output [31:0] out_3,
  output Output
);


  assign out_3 = {in_2[30:0], in_1};
  assign Output = in_2[31];

  // Other names for the same wires on the sheet: a[31:0] = in_2; a____1[31:0] = {in_2[30:0], in_1}
endmodule

module Instruction_Decoder (
  input  [31:0] Instruction,
  output [15:0] Constant,
  output [25:0] Destine,
  output [4:0] RS,
  output [4:0] RT,
  output [4:0] RD,
  output [3:0] ALU_Selector,
  output ADDI,
  output ANDI,
  output ORI,
  output XORI,
  output BLTZ,
  output BEQ,
  output BNE,
  output BLEZ,
  output BGTZ,
  output SLTI,
  output SLTIU,
  output LW,
  output SW,
  output WrHL,
  output Wr,
  output IsALU,
  output Jump,
  output push,
  output pop,
  output mfhi,
  output mflo,
  output jr,
  output nop,
  output halt,
  output tty,
  output rnd,
  output kbd
);

  wire or_1_out;
  wire [3:0] ALU_OP, multiplexer_1_out;
  wire [5:0] Func, Op;

  Instruction_Splitter instruction_splitter_1 (
    .Instruction(Instruction), .FUNC_CODE(Func), .OP_CODE(Op), .Destine(Destine), .Constant(Constant),
    .RD(RD), .RT(RT), .RS(RS));
  Instructions_Control_Flags instructions_control_flags_1 (
    .OPCode(Op), .FuncCode(Func), .ALU(ALU_OP), .IsAlu(IsALU), .WriteEnable(Wr), .Write_Hi_Lo_Enable(WrHL),
    .JUMP(Jump), .ADDI(ADDI), .ANDI(ANDI), .ORI(ORI), .XORI(XORI), .BLTZ(BLTZ), .BEQ(BEQ), .BNE(BNE),
    .BLEZ(BLEZ), .BGTZ(BGTZ), .SLTI(SLTI), .SLTIU(SLTIU), .LW(LW), .SW(SW), .Push(push), .Pop(pop),
    .mfhi(mfhi), .mflo(mflo), .nop(nop), .jr(jr), .halt(halt), .tty(tty), .rnd(rnd), .kbd(kbd));
  Multiplexer #(.width(4), .enable("false")) multiplexer_1 (
    .in0(ALU_OP), .in1(4'b0010), .out(multiplexer_1_out), .sel(or_1_out));
  or or_1 (or_1_out, BLTZ, BEQ, BLEZ, BNE, BGTZ);
  Multiplexer #(.width(4), .enable("false")) multiplexer_2 (
    .in0(multiplexer_1_out), .in1(ALU_OP), .out(ALU_Selector), .sel(IsALU));

  // Other names for the same wires on the sheet: ALU[3:0] = ALU_Selector

  // Notes on the sheet:
  //   output
endmodule

module Instruction_Splitter (
  input  [31:0] Instruction,
  output [5:0] FUNC_CODE,
  output [5:0] OP_CODE,
  output [25:0] Destine,
  output [15:0] Constant,
  output [4:0] RD,
  output [4:0] RT,
  output [4:0] RS
);


  assign Constant = Instruction[15:0];
  assign Destine = Instruction[25:0];
  assign FUNC_CODE = Instruction[5:0];
  assign OP_CODE = Instruction[31:26];
  assign RD = Instruction[15:11];
  assign RS = Instruction[25:21];
  assign RT = Instruction[20:16];

  // Other names for the same wires on the sheet: Jump[25:0] = Instruction[25:0]

  // Notes on the sheet:
  //   Decode
  //   Output
endmodule

module Instructions_Control_Flags (
  input  [5:0] OPCode,
  input  [5:0] FuncCode,
  output [3:0] ALU,
  output IsAlu,
  output WriteEnable,
  output Write_Hi_Lo_Enable,
  output JUMP,
  output ADDI,
  output ANDI,
  output ORI,
  output XORI,
  output BLTZ,
  output BEQ,
  output BNE,
  output BLEZ,
  output BGTZ,
  output SLTI,
  output SLTIU,
  output LW,
  output SW,
  output Push,
  output Pop,
  output mfhi,
  output mflo,
  output nop,
  output jr,
  output halt,
  output tty,
  output rnd,
  output kbd
);

  wire ADDI_t, and_5_out, and_11_out, and_12_out, ANDI_t, BEQ_t, BGTZ_t, BLEZ_t, BLTZ_t, BNE_t,
       comparator_1_eq, comparator_2_eq, comparator_3_eq, comparator_5_eq, comparator_12_eq,
       comparator_13_eq, comparator_16_eq, comparator_17_eq, comparator_18_eq, comparator_19_eq,
       comparator_21_eq, comparator_22_eq, comparator_23_eq, comparator_24_eq, is000xxx, is001xxx, is10xxxx,
       is100xxx, is0110xx, is1010xx, LW_t, mem_reg_func1, mem_reg_func2, mem_reg_op, or_1_out, ORI_t, SLTI_t,
       SLTIU_t, special, SW_t, Type_I, Type_R, XORI_t;
  wire [3:0] ALU_op;

  Comparator_part #(.width(3), .mode("unsigned")) comparator_1 (
    .a(FuncCode[2:0]), .b(3'b011), .eq(comparator_1_eq));  // open: gt, lt
  Comparator_part #(.width(3), .mode("unsigned")) comparator_2 (
    .a(FuncCode[2:0]), .b(3'b001), .eq(comparator_2_eq));  // open: gt, lt
  Comparator_part #(.width(3), .mode("unsigned")) comparator_3 (
    .a(FuncCode[5:3]), .b(3'b100), .eq(comparator_3_eq));  // open: gt, lt
  Comparator_part #(.width(4), .mode("unsigned")) comparator_4 (
    .a(FuncCode[5:2]), .b(4'b0110), .eq(is0110xx));  // open: gt, lt
  Comparator_part #(.width(4), .mode("unsigned")) comparator_5 (
    .a(FuncCode[5:2]), .b(4'b1010), .eq(comparator_5_eq));  // open: gt, lt
  Comparator_part #(.width(3), .mode("unsigned")) comparator_6 (
    .a(OPCode[5:3]), .b(3'b001), .eq(is001xxx));  // open: gt, lt
  Comparator_part #(.width(3), .mode("unsigned")) comparator_7 (
    .a(OPCode[5:3]), .b(3'b000), .eq(is000xxx));  // open: gt, lt
  Comparator_part #(.width(2), .mode("unsigned")) comparator_8 (
    .a(OPCode[5:4]), .b(2'b10), .eq(is10xxxx));  // open: gt, lt
  Comparator_part #(.width(6), .mode("unsigned")) comparator_9 (
    .a(OPCode), .b(6'b111000), .eq(mem_reg_op));  // open: gt, lt
  Comparator_part #(.width(6), .mode("unsigned")) comparator_10 (
    .a(FuncCode), .b(6'b000001), .eq(mem_reg_func1));  // open: gt, lt
  Comparator_part #(.width(6), .mode("unsigned")) comparator_11 (
    .a(FuncCode), .b({6{1'b0}}), .eq(mem_reg_func2));  // open: gt, lt
  Comparator_part #(.width(2)) comparator_12 (.a(FuncCode[1:0]), .b(2'b00), .eq(comparator_12_eq));  // open: gt, lt
  Comparator_part #(.width(2)) comparator_13 (.a(FuncCode[1:0]), .b(2'b01), .eq(comparator_13_eq));  // open: gt, lt
  Comparator_part #(.width(6), .mode("unsigned")) comparator_14 (
    .a(OPCode), .b({6{1'b0}}), .eq(Type_R));  // open: gt, lt
  Comparator_part #(.width(6), .mode("unsigned")) comparator_15 (.a(OPCode), .b(6'b000010), .eq(JUMP));  // open: gt, lt
  nor nor_1 (Type_I, Type_R, JUMP);
  and and_1 (is100xxx, comparator_3_eq, ~comparator_1_eq, ~comparator_2_eq);  // AND_Gate
  and and_2 (is1010xx, ~comparator_12_eq, comparator_5_eq, ~comparator_13_eq);  // AND_Gate
  Demultiplexer #(.select(3), .enable("false")) demultiplexer_1 (
    .out0(ADDI_t), .out2(SLTI_t), .out3(SLTIU_t), .out4(ANDI_t), .out5(ORI_t), .out6(XORI_t), .in(Type_I),
    .sel(OPCode[2:0]));  // open: out1, out7
  and and_3 (Push, mem_reg_op, mem_reg_func1);
  and and_4 (Pop, mem_reg_op, mem_reg_func2);
  or or_1 (or_1_out, is100xxx, is0110xx, is1010xx);
  Multiplexer #(.select(3), .width(4)) multiplexer_1 (
    .in0(4'b0000), .in2(4'b0001), .in4(4'b0010), .in5(4'b0011), .in6(4'b0100), .in7(4'b0101), .out(ALU_op),
    .sel(FuncCode[2:0]), .en(and_5_out));  // open: in1, in3
  and and_5 (and_5_out, is100xxx, IsAlu);
  and and_6 (IsAlu, or_1_out, Type_R);
  Demultiplexer #(.select(3), .enable("false")) demultiplexer_2 (
    .out1(BLTZ_t), .out4(BEQ_t), .out5(BNE_t), .out6(BLEZ_t), .out7(BGTZ_t), .in(Type_I), .sel(OPCode[2:0]));  // open: out0, out2, out3
  Comparator_part #(.width(6), .mode("unsigned")) comparator_16 (
    .a(FuncCode), .b(6'b010000), .eq(comparator_16_eq));  // open: gt, lt
  Comparator_part #(.width(6), .mode("unsigned")) comparator_17 (
    .a(FuncCode), .b(6'b010010), .eq(comparator_17_eq));  // open: gt, lt
  Comparator_part #(.width(6), .mode("unsigned")) comparator_18 (
    .a(FuncCode), .b({6{1'b0}}), .eq(comparator_18_eq));  // open: gt, lt
  Comparator_part #(.width(6), .mode("unsigned")) comparator_19 (
    .a(FuncCode), .b(6'b001000), .eq(comparator_19_eq));  // open: gt, lt
  and and_7 (mfhi, comparator_16_eq, Type_R);
  and and_8 (mflo, comparator_17_eq, Type_R);
  and and_9 (nop, comparator_18_eq, Type_R);
  and and_10 (jr, comparator_19_eq, Type_R);
  Multiplexer #(.select(2), .width(4)) multiplexer_2 (
    .in2(4'b0110), .in3(4'b0111), .out(ALU_op), .sel(FuncCode[1:0]), .en(and_11_out));  // open: in0, in1
  and and_11 (and_11_out, is1010xx, IsAlu);
  and and_12 (and_12_out, IsAlu, ~Write_Hi_Lo_Enable);  // AND_Gate
  Multiplexer #(.width(4), .enable("false")) multiplexer_3 (.in0(4'b1100), .in1(ALU_op), .out(ALU), .sel(IsAlu));
  Demultiplexer #(.select(4), .enable("false")) demultiplexer_3 (
    .out3(LW_t), .out11(SW_t), .in(Type_I), .sel(OPCode[3:0]));  // open: out0, out1, out2, out4, out5, out6, out7, out8, out9, out10, out12, out13, out14, out15
  or or_2 (WriteEnable, and_12_out, is001xxx);
  Comparator_part #(.width(6), .mode("unsigned")) comparator_20 (
    .a(OPCode), .b({6{1'b1}}), .eq(special));  // open: gt, lt
  Comparator_part #(.width(6), .mode("unsigned")) comparator_21 (
    .a(FuncCode), .b({6{1'b1}}), .eq(comparator_21_eq));  // open: gt, lt
  Comparator_part #(.width(6), .mode("unsigned")) comparator_22 (
    .a(FuncCode), .b(6'b000001), .eq(comparator_22_eq));  // open: gt, lt
  Comparator_part #(.width(6), .mode("unsigned")) comparator_23 (
    .a(FuncCode), .b(6'b000010), .eq(comparator_23_eq));  // open: gt, lt
  Comparator_part #(.width(6), .mode("unsigned")) comparator_24 (
    .a(FuncCode), .b(6'b000100), .eq(comparator_24_eq));  // open: gt, lt
  Multiplexer #(.select(2), .width(4)) multiplexer_4 (
    .in0(4'b1000), .in1(4'b1001), .in2(4'b1010), .in3(4'b1011), .out(ALU_op), .sel(FuncCode[1:0]),
    .en(Write_Hi_Lo_Enable));
  and and_13 (Write_Hi_Lo_Enable, is0110xx, IsAlu);
  and and_14 (halt, comparator_21_eq, special);
  and and_15 (tty, comparator_22_eq, special);
  and and_16 (rnd, comparator_23_eq, special);
  and and_17 (kbd, comparator_24_eq, special);
  and and_18 (LW, LW_t, is10xxxx);
  and and_19 (SW, SW_t, is10xxxx);
  and and_20 (ADDI, ADDI_t, is001xxx);
  and and_21 (ANDI, ANDI_t, is001xxx);
  and and_22 (ORI, ORI_t, is001xxx);
  and and_23 (XORI, XORI_t, is001xxx);
  and and_24 (BLTZ, BLTZ_t, is000xxx);
  and and_25 (BEQ, BEQ_t, is000xxx);
  and and_26 (BNE, BNE_t, is000xxx);
  and and_27 (BLEZ, BLEZ_t, is000xxx);
  and and_28 (BGTZ, BGTZ_t, is000xxx);
  and and_29 (SLTI, SLTI_t, is001xxx);
  and and_30 (SLTIU, SLTIU_t, is001xxx);

  // Other names for the same wires on the sheet: _100xxx[2:0] = FuncCode[2:0]; _0110xx[1:0] = FuncCode[1:0];
  //   _1010xx[1:0] = FuncCode[1:0]; Func[5:0] = FuncCode; IsAluOP = IsAlu; _000xxx[2:0] = OPCode[2:0];
  //   _001xxx[2:0] = OPCode[2:0]; _10xxxx[3:0] = OPCode[3:0]; OP[5:0] = OPCode; Type_J = JUMP; Write = WriteEnable;
  //   WriteHiLo = Write_Hi_Lo_Enable

  // Notes on the sheet:
  //   Input Zone
  //   Stack
  //   Type I
  //   Is ALU Operation?
  //   Select Type Operation
  //   Type R
  //   Select Alu operator
  //   Write Enable
  //   especiales
  //   Output Zone
endmodule

module Instruction_Register (
  input  [31:0] Instruction,
  input  Enable,
  input  RST,
  input  Clk,
  output [31:0] Instruction_2
);

  Register #(.width(32)) u_Instruction (.D(Instruction), .en(Enable), .Q(Instruction_2), .clk(Clk), .clr(RST));
endmodule

module Register_File (
  input  [31:0] DataIncome,
  input  [4:0] DataAddress,
  input  [4:0] Selector_A,
  input  [4:0] Selector_B,
  input  [31:0] Hi_in,
  input  [31:0] Lo_in,
  input  Reset,
  input  Clock,
  input  in_9,
  input  WriteEnable,
  output [31:0] OutA,
  output [31:0] OutB,
  output [31:0] Hi_out,
  output [31:0] Lo_out,
  output [31:0] SP
);

  wire Dir1, Dir2, Dir3, Dir4, Dir5, Dir6, Dir7, Dir8, Dir9, Dir10, Dir11, Dir12, Dir13, Dir14, Dir15, Dir16,
       Dir17, Dir18, Dir19, Dir20, Dir21, Dir22, Dir23, Dir24, Dir25, Dir26, Dir27, Dir28, Dir29, Dir30,
       DirSP;
  wire [31:0] out1, out2, out3, out4, out5, out6, out7, out8, out9, out10, out11, out12, out13, out14, out15,
       out16, out17, out18, out19, out20, out21, out22, out23, out24, out25, out26, out27, out28, out29,
       out30;

  Decoder #(.select(5), .disabled(0)) decoder_1 (
    .out1(Dir1), .out2(Dir2), .out3(Dir3), .out4(Dir4), .out5(Dir5), .out6(Dir6), .out7(Dir7), .out8(Dir8),
    .out9(Dir9), .out10(Dir10), .out11(Dir11), .out12(Dir12), .out13(Dir13), .out14(Dir14), .out15(Dir15),
    .out16(Dir16), .out17(Dir17), .out18(Dir18), .out19(Dir19), .out20(Dir20), .out21(Dir21), .out22(Dir22),
    .out23(Dir23), .out24(Dir24), .out25(Dir25), .out26(Dir26), .out27(Dir27), .out28(Dir28), .out29(Dir29),
    .out30(Dir30), .out31(DirSP), .sel(DataAddress), .en(WriteEnable));  // open: out0
  Register #(.width(32)) register_1 (.D(DataIncome), .en(Dir8), .Q(out8), .clk(Clock), .clr(Reset));
  Register #(.width(32)) register_2 (.D(DataIncome), .en(Dir16), .Q(out16), .clk(Clock), .clr(Reset));
  Register #(.width(32)) register_3 (.D(DataIncome), .en(Dir24), .Q(out24), .clk(Clock), .clr(Reset));
  Register #(.width(32)) register_4 (.D(DataIncome), .en(Dir1), .Q(out1), .clk(Clock), .clr(Reset));
  Register #(.width(32)) register_5 (.D(DataIncome), .en(Dir9), .Q(out9), .clk(Clock), .clr(Reset));
  Register #(.width(32)) register_6 (.D(DataIncome), .en(Dir17), .Q(out17), .clk(Clock), .clr(Reset));
  Register #(.width(32)) register_7 (.D(DataIncome), .en(Dir25), .Q(out25), .clk(Clock), .clr(Reset));
  Register #(.width(32)) register_8 (.D(DataIncome), .en(Dir2), .Q(out2), .clk(Clock), .clr(Reset));
  Register #(.width(32)) register_9 (.D(DataIncome), .en(Dir10), .Q(out10), .clk(Clock), .clr(Reset));
  Register #(.width(32)) register_10 (.D(DataIncome), .en(Dir18), .Q(out18), .clk(Clock), .clr(Reset));
  Register #(.width(32)) register_11 (.D(DataIncome), .en(Dir26), .Q(out26), .clk(Clock), .clr(Reset));
  Multiplexer #(.select(5), .width(32), .enable("false")) multiplexer_1 (
    .in0({32{1'b0}}), .in1(out1), .in2(out2), .in3(out3), .in4(out4), .in5(out5), .in6(out6), .in7(out7),
    .in8(out8), .in9(out9), .in10(out10), .in11(out11), .in12(out12), .in13(out13), .in14(out14),
    .in15(out15), .in16(out16), .in17(out17), .in18(out18), .in19(out19), .in20(out20), .in21(out21),
    .in22(out22), .in23(out23), .in24(out24), .in25(out25), .in26(out26), .in27(out27), .in28(out28),
    .in29(out29), .in30(out30), .in31(SP), .out(OutA), .sel(Selector_A));
  Register #(.width(32)) register_12 (.D(DataIncome), .en(Dir3), .Q(out3), .clk(Clock), .clr(Reset));
  Register #(.width(32)) register_13 (.D(DataIncome), .en(Dir11), .Q(out11), .clk(Clock), .clr(Reset));
  Register #(.width(32)) register_14 (.D(DataIncome), .en(Dir19), .Q(out19), .clk(Clock), .clr(Reset));
  Register #(.width(32)) register_15 (.D(DataIncome), .en(Dir27), .Q(out27), .clk(Clock), .clr(Reset));
  Register #(.width(32)) register_16 (.D(DataIncome), .en(Dir4), .Q(out4), .clk(Clock), .clr(Reset));
  Register #(.width(32)) register_17 (.D(DataIncome), .en(Dir12), .Q(out12), .clk(Clock), .clr(Reset));
  Register #(.width(32)) register_18 (.D(DataIncome), .en(Dir20), .Q(out20), .clk(Clock), .clr(Reset));
  Register #(.width(32)) register_19 (.D(DataIncome), .en(Dir28), .Q(out28), .clk(Clock), .clr(Reset));
  Multiplexer #(.select(5), .width(32), .enable("false")) multiplexer_2 (
    .in0({32{1'b0}}), .in1(out1), .in2(out2), .in3(out3), .in4(out4), .in5(out5), .in6(out6), .in7(out7),
    .in8(out8), .in9(out9), .in10(out10), .in11(out11), .in12(out12), .in13(out13), .in14(out14),
    .in15(out15), .in16(out16), .in17(out17), .in18(out18), .in19(out19), .in20(out20), .in21(out21),
    .in22(out22), .in23(out23), .in24(out24), .in25(out25), .in26(out26), .in27(out27), .in28(out28),
    .in29(out29), .in30(out30), .in31(SP), .out(OutB), .sel(Selector_B));
  Register #(.width(32)) register_20 (.D(DataIncome), .en(Dir5), .Q(out5), .clk(Clock), .clr(Reset));
  Register #(.width(32)) register_21 (.D(DataIncome), .en(Dir13), .Q(out13), .clk(Clock), .clr(Reset));
  Register #(.width(32)) register_22 (.D(DataIncome), .en(Dir21), .Q(out21), .clk(Clock), .clr(Reset));
  Register #(.width(32)) register_23 (.D(DataIncome), .en(Dir29), .Q(out29), .clk(Clock), .clr(Reset));
  Register #(.width(32)) register_24 (.D(DataIncome), .en(Dir6), .Q(out6), .clk(Clock), .clr(Reset));
  Register #(.width(32)) register_25 (.D(DataIncome), .en(Dir14), .Q(out14), .clk(Clock), .clr(Reset));
  Register #(.width(32)) register_26 (.D(DataIncome), .en(Dir22), .Q(out22), .clk(Clock), .clr(Reset));
  Register #(.width(32)) register_27 (.D(DataIncome), .en(Dir30), .Q(out30), .clk(Clock), .clr(Reset));
  Register #(.width(32)) register_28 (.D(DataIncome), .en(Dir7), .Q(out7), .clk(Clock), .clr(Reset));
  Register #(.width(32)) register_29 (.D(DataIncome), .en(Dir15), .Q(out15), .clk(Clock), .clr(Reset));
  Register #(.width(32)) register_30 (.D(DataIncome), .en(Dir23), .Q(out23), .clk(Clock), .clr(Reset));
  Register #(.width(32)) register_31 (.D(DataIncome), .en(DirSP), .Q(SP), .clk(Clock), .clr(Reset));
  Register #(.width(32)) register_32 (.D(Hi_in), .en(in_9), .Q(Hi_out), .clk(Clock), .clr(Reset));
  Register #(.width(32)) register_33 (.D(Lo_in), .en(in_9), .Q(Lo_out), .clk(Clock), .clr(Reset));

  // Other names for the same wires on the sheet: Clk = Clock; DA[4:0] = DataAddress; DataInc[31:0] = DataIncome;
  //   DHi[31:0] = Hi_in; DLo[31:0] = Lo_in; outHi[31:0] = Hi_out; outLo[31:0] = Lo_out; outSP[31:0] = SP; RST = Reset;
  //   SelectA[4:0] = Selector_A; SelectB[4:0] = Selector_B; WEnable = WriteEnable; WriteHiLo = in_9

  // Notes on the sheet:
  //   Register Input
  //   Configuration Inputs
  //   Registers
  //   WRITE
  //   READ
  //   Hi Lo Registers
  //   Hi
  //   Lo
  //   Output Zone
endmodule

module Memory_Control (
  input  [3:0] in_1,
  input  [3:0] in_2,
  input  in_3,
  input  in_4,
  input  [31:0] in_5,
  input  in_6,
  input  in_7,
  input  in_8,
  input  in_9,
  input  [31:0] in_10,
  input  [31:0] in_11,
  input  [31:0] in_12,
  input  [31:0] in_13,
  output [31:0] Output,
  output [31:0] Output_2,
  output [31:0] Output_3,
  output [31:0] Output_4,
  output [15:0] Output_5,
  output [3:0] Output_6,
  output Output_7,
  output Output_8,
  output Output_9,
  output Output_10,
  output Output_11
);

  wire CSD, CSI, or_1_out, stop;
  wire [31:0] DO0, DO1, DO2, DO3, IO0, IO1, IO2, IO3;

  or or_1 (or_1_out, in_6, stop);
  RAM_Read ram_read_1 (
    .in_5(in_5), .in_6(in_10), .in_7(in_11), .in_8(in_12), .in_1(in_1), .in_3(in_4), .in_4(in_7),
    .Output_3(IO0), .Output_4(IO1), .Output_5(IO2), .Output_6(IO3), .Output(CSI), .Output_2(Output_9),
    .in_2(in_3));
  D_Flip_Flop #(.trigger("falling")) d_ff_1 (
    .clk(in_3), .D(in_6), .Q(Output_8), .en(or_1_out));  // open: Qn, preset, reset
  Delay delay_1 (.in_1(Output_8), .in_2(Output_11), .in_3(in_3), .in_4(in_2), .Output(stop));
  Multiplexer #(.width(32), .enable("false")) multiplexer_1 (
    .in0({DO0[7:0], DO0[15:8], DO0[23:16], DO0[31:24]}), .in1(IO0), .out(Output), .sel(in_9));
  Multiplexer #(.width(32), .enable("false")) multiplexer_2 (
    .in0({DO2[7:0], DO2[15:8], DO2[23:16], DO2[31:24]}), .in1(IO2), .out(Output_3), .sel(in_9));
  RAM_Read ram_read_2 (
    .in_5(in_5), .in_6(in_10), .in_7(in_11), .in_8(in_12), .in_1(in_1), .in_3(in_4), .in_4(in_8),
    .Output_3(DO0), .Output_4(DO1), .Output_5(DO2), .Output_6(DO3), .Output(CSD), .Output_2(Output_10),
    .in_2(in_3));
  D_Flip_Flop #(.trigger("falling")) d_ff_2 (.clk(in_3), .D(stop), .Q(Output_11));  // open: Qn, preset, en, reset
  Multiplexer #(.width(32), .enable("false")) multiplexer_3 (
    .in0({DO1[7:0], DO1[15:8], DO1[23:16], DO1[31:24]}), .in1(IO1), .out(Output_2), .sel(in_9));
  Multiplexer #(.width(32), .enable("false")) multiplexer_4 (
    .in0({DO3[7:0], DO3[15:8], DO3[23:16], DO3[31:24]}), .in1(IO3), .out(Output_4), .sel(in_9));
  Demultiplexer #(.select(2), .enable("false")) demultiplexer_1 (
    .out0(Output_6[0]), .out1(Output_6[1]), .out2(Output_6[2]), .out3(Output_6[3]), .in(1'b1),
    .sel(in_13[3:2]));
  or or_2 (Output_7, CSD, CSI, Output_8);

  assign Output_5 = in_13[19:4];

  // Other names for the same wires on the sheet: bank0[31:0] = in_5; bank1[31:0] = in_10; bank2[31:0] = in_11;
  //   bank3[31:0] = in_12; clock = in_3; CS = Output_7; DP_address[31:0] = in_13; ADDR[15:0] = in_13[19:4];
  //   get_data = in_8; get_inst = in_7; is_inst = in_9; MASK[3:0] = Output_6; out_bank0[31:0] = Output;
  //   out_bank1[31:0] = Output_2; out_bank2[31:0] = Output_3; out_bank3[31:0] = Output_4; read_time[3:0] = in_1;
  //   ready_data = Output_10; ready_inst = Output_9; ready_write = Output_11; reset = in_4; RW = Output_8;
  //   write = in_6; write_time[3:0] = in_2
endmodule

module RAM_Read (
  input  [3:0] in_1,
  input  in_2,
  input  in_3,
  input  in_4,
  input  [31:0] in_5,
  input  [31:0] in_6,
  input  [31:0] in_7,
  input  [31:0] in_8,
  output Output,
  output Output_2,
  output [31:0] Output_3,
  output [31:0] Output_4,
  output [31:0] Output_5,
  output [31:0] Output_6
);

  wire a, enable, or_1_out, stop;

  D_Flip_Flop #(.trigger("falling")) d_ff_1 (.clk(in_2), .D(in_4), .Q(a), .en(or_1_out));  // open: Qn, preset, reset
  or or_1 (or_1_out, in_4, stop);
  Delay delay_1 (.in_1(a), .in_2(Output_2), .in_3(in_2), .in_4(in_1), .Output(stop));
  Register #(.width(32)) register_1 (.D(in_5), .en(enable), .Q(Output_3), .clk(in_2), .clr(in_3));
  Register #(.width(32)) register_2 (.D(in_7), .en(enable), .Q(Output_5), .clk(in_2), .clr(in_3));
  or or_2 (Output, a, enable);
  D_Flip_Flop #(.trigger("falling")) d_ff_2 (
    .clk(in_2), .D(stop), .Q(enable), .reset(Output_2));  // open: Qn, preset, en
  Register #(.width(32)) register_3 (.D(in_6), .en(enable), .Q(Output_4), .clk(in_2), .clr(in_3));
  Register #(.width(32)) register_4 (.D(in_8), .en(enable), .Q(Output_6), .clk(in_2), .clr(in_3));
  D_Flip_Flop #(.trigger("falling")) d_ff_3 (.clk(in_2), .D(enable), .Q(Output_2));  // open: Qn, preset, en, reset

  // Other names for the same wires on the sheet: bank0[31:0] = in_5; bank1[31:0] = in_6; bank2[31:0] = in_7;
  //   bank3[31:0] = in_8; chip_select = Output; clock = in_2; get = in_4; out_bank0[31:0] = Output_3;
  //   out_bank1[31:0] = Output_4; out_bank2[31:0] = Output_5; out_bank3[31:0] = Output_6; read_time[3:0] = in_1;
  //   ready = Output_2; reset = in_3
endmodule

module Delay (
  input  in_1,
  input  in_2,
  input  in_3,
  input  [3:0] in_4,
  output Output
);

  wire [3:0] counter_1_q;

  Counter #(.width(4), .max('hf)) counter_1 (
    .count(in_1), .Q(counter_1_q), .clk(in_3), .clr(in_2));  // open: load, D, carry
  Comparator_part #(.width(4)) comparator_1 (.a(in_4), .b(counter_1_q), .eq(Output));  // open: gt, lt

  // Other names for the same wires on the sheet: clock = in_3; ready = Output; reset = in_2; start = in_1;
  //   wait_time[3:0] = in_4
endmodule
